# Fritzing sketch Handle Fritzing Diagram (saved by Fritzing 0.9.3b)
breadboards: 1

parts:
  Part1 = Arduino Nano (Rev3.0)
  Part2 = InvenSense MPU6050
  Part3 = Bluetooth HC-05 Macho
  VCC1 = Battery block 9V
  R1 = Resistor [tolerance=±5% resistance=100 package="0402 [SMD]"]
  C2 = Capacitor Polarized [package=panasonic_c]
  S2 = Toggle Switch [package=THT]

nets:
  N1: Part1.D1/TX, Part3.RXD
  N2: Part1.D0/RX, Part3.TXD
  GND: Part1.GND, Part3.GND, VCC1.-
  N3: Part1.D2, Part2.INT
  VCC: Part1.VIN, Part2.VCC, Part3.VCC, C2.+, S2.COM
  N4: Part1.A4, Part2.SCL
  N5: Part1.A3, Part2.SDA
  N6: Part2.GND, R1.Pin_1, C2.-
  N7: VCC1.+, S2.L1
  N8: R1.Pin_0, S2.L2
